// Logisim project MiniRISCV.circ as structural Verilog: 5 circuits, main circuit main
module main (
  input  in_1,
  input  in_2,
  input  in_3,
  output [31:0] out_4
);

  wire clock_1_out, control_1_useimm, registerfile_1_p1, registerfile_1_p7;
  wire [3:0] control_1_aluop;
  wire [4:0] control_1_rd, control_1_rs1, control_1_rs2, sa_1_out_2;
  wire [31:0] control_1_imm, multiplexer_1_out, registerfile_1_p8, risc_vprogramrom_1_p2;

  PC pc_1 (.we(in_2), .clk(clock_1_out), .clr(in_3), .out_4(out_4));
  Clock clock_1 (.out(clock_1_out));
  // RISC_VProgramROM risc_vprogramrom_1: pin names not known; wires that end beside it: out_4, risc_vprogramrom_1_p2
  Control control_1 (
    .inst(risc_vprogramrom_1_p2), .rs1(control_1_rs1), .rs2(control_1_rs2), .rd(control_1_rd),
    .imm(control_1_imm), .useImm(control_1_useimm), .ALUop(control_1_aluop));
  // RegisterFile registerfile_1: pin names not known; wires that end beside it: registerfile_1_p1, clock_1_out, in_1, control_1_rd, control_1_rs1, control_1_rs2, registerfile_1_p7, registerfile_1_p8
  Multiplexer #(.width(32), .enable("false")) multiplexer_1 (
    .in0(registerfile_1_p8), .in1(control_1_imm), .out(multiplexer_1_out), .sel(control_1_useimm));
  SA sa_1 (.SA_32(multiplexer_1_out), .out_2(sa_1_out_2));
  // ALU alu_1: pin names not known; wires that end beside it: registerfile_1_p7, multiplexer_1_out, control_1_aluop, sa_1_out_2, registerfile_1_p1, clock_1_out

  // Notes on the sheet:
  //   contents of risc_vprogramrom_1 (hex, n*v repeats v):
  //   lui t1, 1 srli t1, t1, 12  add t2, t1, t0 # t2 = t1 +t0  addi t0, t1, 0 # t0 = t1 + 0 addi t1, t2, 0
  //   # t1 = t2 + 0 add t2, t1, t0 # t2 = t1 +t0  addi t0, t1, 0 # t0 = t1 + 0 addi t1, t2, 0 # t1 = t2 +
  //   0 add t2, t1, t0 # t2 = t1 +t0  addi t0, t1, 0 # t0 = t1 + 0 addi t1, t2, 0 # t1 = t2 + 0 add t2,
  //   t1, t0 # t2 = t1 +t0  addi a0, t2, 0
endmodule

module PC (
  input  we,
  input  clk,
  input  clr,
  output [31:0] out_4
);

  wire incrementer_1_p2, incrementer_2_p1, incrementer_3_p1;
  wire [31:0] incrementer_4_p1;

  Register #(.width(32)) clk_in (.D(incrementer_4_p1), .en(we), .clk(clk), .Q(out_4), .clr(clr));
  // Incrementer #(.width(32)) incrementer_1: pin names not known; wires that end beside it: out_4, incrementer_1_p2, incrementer_1_p2
  // Incrementer #(.width(32)) incrementer_2: pin names not known; wires that end beside it: incrementer_2_p1, incrementer_2_p1
  // Incrementer #(.width(32)) incrementer_3: pin names not known; wires that end beside it: incrementer_3_p1, incrementer_3_p1
  // Incrementer #(.width(32)) incrementer_4: pin names not known; wires that end beside it: incrementer_4_p1
endmodule

module Control (
  input  [31:0] inst,
  output [4:0] rs1,
  output [4:0] rs2,
  output [4:0] rd,
  output [31:0] imm,
  output useImm,
  output [3:0] ALUop
);

  // Decode_Black_Box decode_black_box_1: pin names not known; wires that end beside it: inst, rs1, rs2, rd, imm, useImm, ALUop
endmodule

module SA (
  input  [31:0] SA_32,
  output [4:0] out_2
);


  assign out_2 = SA_32[4:0];
endmodule

module mem (
  input  store,
  input  [3:0] sel_bit,
  input  load,
  input  clear
);

  RAM ram_1 ();  // open: addr, data, sel, clk, ld, clr
endmodule
